# Fritzing sketch Boat_volt_mon4 (saved by Fritzing 0.9.3b)
stripboards: 1

parts:
  WeMos_D1_Mini1 = WeMos D1 Mini
  J2 = female pin header, 8 pins [form="♀ (female)"]
  J3 = female pin header, 8 pins [form="♀ (female)"]
  J4 = Screw terminal - 2 pins [package=THT]
  J19 = single row smd female pin header, 4 pins [form="♀ (female)"]
  J19_2 = single row smd female pin header, 4 pins [form="♀ (female)"]
  J5 = female pin header, 10 pins [form="♀ (female)"]
  C1 = Ceramic Capacitor [capacitance=100nF package="100 mil [THT, multilayer]"]
  C2 = Electrolytic Capacitor [capacitance=0.1mF package="100 mil [THT, electrolytic]"]
  R7 = TRIMPOT [package=3362u-2]
  J20 = Screw terminal - 2 pins [package=THT]

nets:
  N1: WeMos_D1_Mini1.3V3, J3.pin1
  N2: WeMos_D1_Mini1.5V, J2.pin1, J19.pin4, J5.pin10, C1.0, C2.+
  N3: WeMos_D1_Mini1.D1, J2.pin6, J5.pin8
  N4: WeMos_D1_Mini1.D2, J2.pin5, J5.pin7
  N5: WeMos_D1_Mini1.G, J2.pin2, J19.pin1, J5.pin6, J5.pin9, C1.1, C2.-, R7.CCW
  N6: J4.pin1, J19_2.pin4, R7.CW
  N7: J4.pin2, J19_2.pin1
  N8: J5.pin1, J20.pin1
  N9: J5.pin2, J20.pin2
  N10: J5.pin3, R7.WIPER

notes:
  ~/Arduino/Boat_volt_mon4.fzz
  ~/Arduino/Boat_volt_mon4
  ~/ESP/ ard 64 1.8.8
  @larryl@tcls.com 2019
  Adjustable buck set to 5v
  ADS1115
  4 ch AtoD
  diff input from shunt
  12v
  VDD
