# Fritzing sketch ESP_fridge_temp_two (saved by Fritzing 0.9.3b)
stripboards: 2

parts:
  WeMos_D1_Mini1 = WeMos D1 Mini
  J2 = female pin header, 8 pins [form="♀ (female)"]
  J3 = female pin header, 8 pins [form="♀ (female)"]
  R1 = Resistor [tolerance=±5% resistance=1k package=THT]  # not connected
  J4 = Screw terminal - 2 pins [package=THT]
  VCC1 = Battery  # not connected
  R3 = Resistor [tolerance=±5% resistance=4.7k package=THT]  # not connected
  J5 = female pin header, 5 pins [form="♀ (female)"]
  DS1 = DS18B20 1-Wire Temperature Sensor [part_number=DS18B20]  # not connected
  R4 = Resistor [tolerance=±5% resistance=220k package=THT]  # not connected
  J6 = female pin header, 8 pins [form="♀ (female)"]  # not connected
  J7 = female pin header, 8 pins [form="♀ (female)"]  # not connected
  J8 = female pin header, 8 pins [form="♀ (female)"]
  J9 = female pin header, 8 pins [form="♀ (female)"]  # not connected
  J10 = female pin header, 8 pins [form="♀ (female)"]  # not connected
  J11 = female pin header, 8 pins [form="♀ (female)"]
  J12 = female pin header, 5 pins [form="♀ (female)"]
  J13 = female alternating pin header, 3 pins [form="♀ (female)"]
  J15 = female alternating pin header, 3 pins [form="♀ (female)"]
  J16 = male alternating pin header, 2 pins [form="♂ (male)"]
  J17 = male alternating pin header, 2 pins [form="♂ (male)"]
  DS2 = DS18B20 1-Wire Temperature Sensor [part_number=DS18B20]
  S1 = Toggle Switch [package=THT]
  Q1 = MOSFET-NCHANNEL [package=to220v]
  J18 = Piezo Speaker
  R6 = Resistor [tolerance=±5% resistance=4.7k package=THT]

nets:
  N1: WeMos_D1_Mini1.3V3, J3.pin1
  N2: WeMos_D1_Mini1.5V, J2.pin1
  N3: WeMos_D1_Mini1.A0, J3.pin7
  N4: WeMos_D1_Mini1.D0, J3.pin6
  N5: WeMos_D1_Mini1.D1, J2.pin6, J5.pin3
  N6: WeMos_D1_Mini1.D2, J5.pin2
  N7: WeMos_D1_Mini1.D6, J3.pin4
  N8: WeMos_D1_Mini1.RST, J3.pin8
  N9: J2.pin7, J2.pin8
  N10: J4.pin2, J5.pin5
  N11: J8.pin1, J12.pin1, J15.pin1, J16.pin2, J17.pin2, DS2.VDD, J18.pin2, R6.Pin_0
  N12: J8.pin2, J15.pin2, DS2.DQ, R6.Pin_1
  N13: J8.pin4, Q1.G
  N14: J8.pin5, S1.COM
  N15: J8.pin8, S1.L2
  N16: J11.pin1, J12.pin5, J13.pin1, J15.pin3, J16.pin1, J17.pin1, DS2.GND, Q1.S
  N17: J11.pin5, J12.pin2
  N18: J11.pin6, J12.pin3
  N19: J11.pin7, J12.pin4, J13.pin2
  N20: J11.pin8, J13.pin3
  N21: Q1.D, J18.pin1

notes:
  ~/ESP/ESP_fridge_temp.fzz
  ~/Arduino/fridge.ino
  ~/ESP/ ard 64 1.8.1
  @larryl@tcls.com 2017
  3DCnG
  RTC
  DS3231
  Single
  Li-ion 18650 3.7v
  New board wit buzzer. Bad idea as pins are undef during sleep, so it chirpped and buzzed all time.
  Waterproof DS18B20
